# Fritzing sketch air-sensor (saved by Fritzing 0.9.4)
circuit board: 12.1062cm x 4.2146cm
breadboards: 1

parts:
  Mod1 = SDS011 - dust sensor [part_number=1]
  WeMos_D1_Mini1 = WeMos D1 Mini
  LCD1 = LCD screen

nets:
  5V: Mod1.5V, WeMos_D1_Mini1.5V, LCD1.LED+
  GND: Mod1.GND, WeMos_D1_Mini1.G, LCD1.VSS, LCD1.V0, LCD1.R/W, LCD1.LED-
  N1: Mod1.RXD, WeMos_D1_Mini1.TX
  N2: Mod1.TXD, WeMos_D1_Mini1.RX
  3V3: WeMos_D1_Mini1.3V3, LCD1.VDD
  N3: WeMos_D1_Mini1.D0, LCD1.RS
  N4: WeMos_D1_Mini1.D1, LCD1.E
  N5: WeMos_D1_Mini1.D5, LCD1.DB4
  N6: WeMos_D1_Mini1.D6, LCD1.DB5
  N7: WeMos_D1_Mini1.D7, LCD1.DB6
  N8: WeMos_D1_Mini1.D8, LCD1.DB7

custom parts:
  SDS011 - dust sensor: The SDS 011 Sensor is a quite recent Air Quality Sensor developed by inovafit, a spin-off from the university of Jinan (in Shandong). With its size, it is probably one of the best sensor in terms of accuracy: While other sensors tend to focus on shrinking the sensor size, the SDS 011 has opted for a size tradeoff allowing it to use a larger fan. And the larger the fan, the better the quality.
  WeMos D1 Mini: The D1 mini is a mini wifi board based on ESP-8266EX.
